# Fritzing sketch cronowork (saved by Fritzing 0.7.6b)
breadboards: 1

parts:
  LCD1 = Adafruit Negative RGB 2x16 LCD
  U1 = atmega328 [package=dip]
  XTAL1 = Crystal [frequency="16 Mhz" package=THT]
  VCC1 = Battery
  J1 = female pin header, 2 pins [form="♀ (female)"]
  POT1 = Breadboard Trimpot
  J2 = male pin header, 12 pins [form="♂ (male)"]
  C1 = Ceramic Capacitor [capacitance=100nF package="100 mil [THT, multilayer]"]
  C2 = Ceramic Capacitor [capacitance=100nF package="100 mil [THT, multilayer]"]
  CONN1 = USB connector [package=THT]
  R1 = Resistor [tolerance=±5% resistance=10k package=THT]
  J4 = Piezo Speaker
  R2 = Resistor [tolerance=±5% resistance=220 package=THT]
  J3 = screw terminal, 3 pins

nets:
  GND: LCD1.no_name_yet#0, LCD1.no_name_yet#4, U1.GND, VCC1.-, J1.pin1, POT1.PIN1, J2.pin9, J2.pin12, C1.1, C2.0, CONN1.GND, CONN1.chassis6, R1.Pin_0, J4.pin2, J3.pin2
  N1: LCD1.no_name_yet#1, LCD1.no_name_yet#14, U1.VCC, U1.AVCC, U1.AREF, VCC1.+, POT1.PIN3, J2.pin11, J3.pin1
  N2: LCD1.no_name_yet#2, POT1.PIN2
  N3: LCD1.no_name_yet#3, U1.A2, J2.pin10
  N4: LCD1.no_name_yet#5, U1.A1, J2.pin8
  N5: LCD1.no_name_yet#10, U1.A0, J2.pin7
  N6: LCD1.no_name_yet#11, U1.D13, J2.pin6
  N7: LCD1.no_name_yet#12, U1.D12, J2.pin5
  N8: LCD1.no_name_yet#13, U1.D11_(PWM), J2.pin4
  N9: LCD1.no_name_yet#15, U1.D10_(PWM), J2.pin3
  N10: LCD1.no_name_yet#16, U1.D9_(PWM), J2.pin2
  N11: LCD1.no_name_yet#17, U1.D8, J2.pin1
  N12: U1.D2, CONN1.5V, R1.Pin_1, J3.pin3
  N13: U1.D3_(PWM), R2.Pin_0
  N14: U1.XLAT1, XTAL1.pin_0, C1.0
  N15: U1.XLAT2, XTAL1.pin_1, C2.1
  N16: U1.A3, J1.pin2
  N17: J4.pin1, R2.Pin_1

notes:
  Cronowork, Cronómetro basado en arduino para control de tiempos en  diferentes tareas de trabajo. LICENCIA BSD, 3

custom parts:
  Adafruit Negative RGB 2x16 LCD: Adafruit Negative 2x16 LCD Display with RGB Backlight
